# Fritzing sketch gy521-servo (saved by Fritzing 0.9.3b)
breadboards: 1

parts:
  U1 = NodeMCU V1.0
  GY1 = MPU-6050 Board GY-521 [form="♀ (female)" package=THT]
  Eixo_Y = Basic Servo
  Eixo_X = Basic Servo

nets:
  N1: U1.D1, GY1.pin3
  N2: U1.D2, GY1.pin4
  VCC: U1.3V3, GY1.pin1, Eixo_Y.vcc, Eixo_X.vcc
  GND: U1.GND, GY1.pin2, Eixo_Y.gnd, Eixo_X.gnd
  N3: U1.D5, Eixo_X.pulse
  N4: U1.D6, Eixo_Y.pulse

custom parts:
  NodeMCU V1.0: ESP8266 based NodeMCU
  MPU-6050 Board GY-521: Acelerometro y Giroscopio MPU-6050 Board GY-521
